// Logisim project Circuito.circ as structural Verilog: 3 circuits, main circuit main
module main (
  input  [31:0] x0,
  input  [1:0] sel,
  input  rst_n,
  output [31:0] o_y0
);

  wire clk_out, not_1_out;
  wire [31:0] despl_1_out_2, multiplexer_1_out, multiplexer_2_out, multiplexer_3_out, sumador_1_out_6, x0_t,
       x1, x2, x3, y1;

  Clock clk (.out(clk_out));
  not not_1 (not_1_out, rst_n);
  Register #(.width(32)) u_x1 (.D(multiplexer_1_out), .clk(clk_out), .Q(x1), .clr(not_1_out));  // open: en
  Multiplexer #(.select(2), .width(32)) multiplexer_1 (
    .in0(x0), .in1(x2), .in2(x0), .in3(x0), .out(multiplexer_1_out), .sel(sel));
  Sumador sumador_1 (.in_1(x0_t), .in_2(x1), .in_3(x2), .in_4(x3), .in_5(y1), .out_6(sumador_1_out_6));
  Register #(.width(32)) u_x2 (.D(multiplexer_2_out), .clk(clk_out), .Q(x2), .clr(not_1_out));  // open: en
  Multiplexer #(.select(2), .width(32)) multiplexer_2 (
    .in0(x1), .in1(x0), .in2(x2), .in3(x2), .out(multiplexer_2_out), .sel(sel));
  despl despl_1 (.in_1(sumador_1_out_6), .out_2(despl_1_out_2));
  Register #(.width(32)) y0 (.D(despl_1_out_2), .clk(clk_out), .Q(o_y0), .clr(not_1_out));  // open: en
  Register #(.width(32)) u_x3 (.D(multiplexer_3_out), .clk(clk_out), .Q(x3), .clr(not_1_out));  // open: en
  Multiplexer #(.select(2), .width(32)) multiplexer_3 (
    .in0(x2), .in1(x1), .in2(x3), .in3(x3), .out(multiplexer_3_out), .sel(sel));
  Register #(.width(32)) u_y1 (.D(o_y0), .clk(clk_out), .Q(y1), .clr(not_1_out));  // open: en

  // Other names for the same wires on the sheet: y0[31:0] = o_y0
endmodule

module Sumador (
  input  [31:0] in_1,
  input  [31:0] in_2,
  input  [31:0] in_3,
  input  [31:0] in_4,
  input  [31:0] in_5,
  output [31:0] out_6
);


  assign out_6 = in_1;
endmodule

module despl (
  input  [31:0] in_1,
  output [31:0] out_2
);


  assign out_2 = in_1;
endmodule
